# Fritzing sketch LoRa (saved by Fritzing 0.9.4)

parts:
  Part1 = Adafruit Feather M0 RFM9x LoRa [part_number="Adafruit #3178 or #3179"]
  Antenna1 = HC-12 Antenna
  DHT1 = DHT22 Humidity and Temperature Sensor
  R1 = Resistor [tolerance=±5% resistance=220 package=THT]

nets:
  N1: Part1.ANT, Antenna1.ANT
  GND: Part1.GND, DHT1.GND
  +3V3: Part1.+3V3, DHT1.VDD, R1.Pin_0
  N2: Part1.D5, DHT1.DATA, R1.Pin_1

custom parts:
  Adafruit Feather M0 RFM9x LoRa: This is the Adafruit Feather M0 RFM95 LoRa Radio - our take on an microcontroller with a "Long Range (LoRa)" packet radio transceiver with built in USB and battery charging. Its an Adafruit Feather M0 with a 433Mhz or 900MHz radio module cooked in! Great for making wireless networks that are more flexible than Bluetooth LE and without the high power requirements of WiFi. We have other boards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
  HC-12 Antenna: Antenna for HC-12 433Mhz Module
