# Fritzing sketch arduino_mega_hc_12 (saved by Fritzing 0.9.4)

parts:
  Part1 = Arduino Mega 2560 (Rev3)
  HC-1 = HC-12 Module
  Antenna1 = HC-12 Antenna

nets:
  3V3: Part1.3V3, HC-1.VCC
  GND: Part1.GND, HC-1.GND
  N1: Part1.D0_RX0, HC-1.TXD
  N2: Part1.D1_TX0, HC-1.RXD
  N3: HC-1.ANT, Antenna1.ANT

custom parts:
  HC-12 Module: HC-12 433Mhz Module
  HC-12 Antenna: Antenna for HC-12 433Mhz Module
