# Fritzing sketch arduino_mega_nrf24 (saved by Fritzing 0.9.4)

parts:
  Part1 = Arduino Mega 2560 (Rev3)
  Part2 = NRF24L01+ Breakout Board
  Part5 = Arduino Fio (Funnel I/O)
  Part6 = XBee Pro RF module  # not connected
  Part7 = Adafruit Feather M0 RFM9x LoRa [part_number="Adafruit #3178 or #3179"]
  Antenna2 = HC-12 Antenna
  HC-2 = HC-12 Module
  Antenna3 = HC-12 Antenna
  MCU1 = Raspberry Pi Zero  # not connected

nets:
  GND: Part1.GND, Part2.GND, HC-2.GND
  N1: Part1.D13_PWM, Part7.D0
  N2: Part1.D12_PWM, Part7.D1
  N3: Part1.D11_PWM, Part5.D1/TXO
  N4: Part1.D10_PWM, Part5.D0/RXI
  N5: Part1.D8_PWM, Part2.CS
  3V3: Part1.3V3, Part2.VCC
  5V: Part1.5V, HC-2.VCC
  N6: Part1.D2_PWM, HC-2.RXD
  N7: Part1.D3_PWM, HC-2.TXD
  N8: Part1.D7_PWM, Part2.CE
  N9: Part1.D50, Part2.MISO
  N10: Part1.D51, Part2.MOSI
  N11: Part1.D52, Part2.SCK
  N12: Part7.ANT, Antenna2.ANT
  N13: HC-2.ANT, Antenna3.ANT

custom parts:
  Adafruit Feather M0 RFM9x LoRa: This is the Adafruit Feather M0 RFM95 LoRa Radio - our take on an microcontroller with a "Long Range (LoRa)" packet radio transceiver with built in USB and battery charging. Its an Adafruit Feather M0 with a 433Mhz or 900MHz radio module cooked in! Great for making wireless networks that are more flexible than Bluetooth LE and without the high power requirements of WiFi. We have other boards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
  HC-12 Antenna: Antenna for HC-12 433Mhz Module
  HC-12 Module: HC-12 433Mhz Module
