# Fritzing sketch arduino_mega_xbee (saved by Fritzing 0.9.4)

parts:
  Part1 = XBee Pro RF module  # not connected
  Part4 = Arduino Fio (Funnel I/O)
  Part5 = Arduino Mega 2560 (Rev3)

nets:
  N1: Part4.D0/RXI, Part5.D16_PWM/TX2
  N2: Part4.D1/TXO, Part5.D17_PWM/RX2
