# Fritzing sketch arduino_uno_hc_12 (saved by Fritzing 0.9.4)

parts:
  Part1 = Arduino Uno (Rev3)
  HC-1 = HC-12 Module
  Antenna1 = HC-12 Antenna
  DHT1 = DHT22 Humidity and Temperature Sensor
  R1 = Resistor [tolerance=±5% resistance=220 package=THT]

nets:
  GND: Part1.GND, HC-1.GND, DHT1.GND
  N1: Part1.D0/RX, HC-1.TXD
  N2: Part1.D1/TX, HC-1.RXD
  N3: Part1.D2, DHT1.DATA, R1.Pin_1
  3V3: Part1.3V3, HC-1.VCC
  5V: Part1.5V, DHT1.VDD, R1.Pin_0
  N4: HC-1.ANT, Antenna1.ANT

custom parts:
  HC-12 Module: HC-12 433Mhz Module
  HC-12 Antenna: Antenna for HC-12 433Mhz Module
