# Fritzing sketch arduino_uno_nrf24 (saved by Fritzing 0.9.4)

parts:
  Part1 = NRF24L01+ Breakout Board
  Part2 = Arduino Uno (Rev3)
  DHT1 = DHT22 Humidity and Temperature Sensor
  R1 = Resistor [tolerance=±5% resistance=10k package=THT]

nets:
  GND: Part1.GND, Part2.GND, DHT1.GND
  VCC: Part1.VCC, Part2.3V3
  N1: Part1.CE, Part2.D7
  N2: Part1.CS, Part2.D8
  N3: Part1.SCK, Part2.D12/MISO
  N4: Part1.MOSI, Part2.D11_PWM/MOSI
  N5: Part1.MISO, Part2.D13/SCK
  N6: Part2.D2, DHT1.DATA, R1.Pin_1
  5V: Part2.5V, DHT1.VDD, R1.Pin_0
