# Fritzing sketch arduino_uno_xbee (saved by Fritzing 0.9.4)

parts:
  Part1 = Arduino Uno (Rev3)
  Part2 = XBee Pro RF module

nets:
  N1: Part1.D0/RX, Part2.DOUT
  N2: Part1.D1/TX, Part2.DIN
  3V3: Part1.3V3, Part2.VCC
  GND: Part1.GND, Part2.GND
