# Fritzing sketch arduino_xbee (saved by Fritzing 0.9.4)

parts:
  Part1 = XBee Pro RF module  # not connected
  Part4 = Arduino Fio (Funnel I/O)
  DHT1 = DHT22 Humidity and Temperature Sensor
  R1 = Resistor [tolerance=±5% resistance=220 package=THT]

nets:
  VCC: Part4.VCC, DHT1.VDD, R1.Pin_0
  GND: Part4.GND, DHT1.GND
  N1: Part4.D2, DHT1.DATA, R1.Pin_1
